# Fritzing sketch chematic (saved by Fritzing 0.9.2b)
breadboards: 1

parts:
  Часть1 = Arduino Nano (Rev3.0)
  R1 = Resistor [tolerance=±5% resistance=220 package=THT]
  R2 = Resistor [tolerance=±5% resistance=220 package=THT]
  R3 = Resistor [tolerance=±5% resistance=220 package=THT]
  R4 = Resistor [tolerance=±5% resistance=220 package=THT]
  R5 = Resistor [tolerance=±5% resistance=220 package=THT]
  LED1 = LED - 5mm [color="Red (633nm)" package="5 mm [THT]"]
  LED2 = LED - 5mm [color="Red (633nm)" package="5 mm [THT]"]
  LED3 = LED - 5mm [color="Red (633nm)" package="5 mm [THT]"]
  LED4 = LED - 5mm [color="Red (633nm)" package="5 mm [THT]"]
  LED5 = LED - 5mm [color="Red (633nm)" package="5 mm [THT]"]
  Nokia_5110_LCD_Module1 = Nokia5110LCDModule
  IR_Reciever_(TSOP22)1 = IR Reciever
  Часть3 = Real Time Clock Module - DS1307 RTC Breakout Board
  T1 = DS18B20 Temperature Sensor [part_number=DS18B20 package="TO92 [THT]"]
  R6 = Resistor [tolerance=±5% resistance=4.7k package=THT]

nets:
  GND: Часть1.GND, Nokia_5110_LCD_Module1.Grnd, IR_Reciever_(TSOP22)1.GND, Часть3.GND, T1.GND
  N1: Часть1.D7, IR_Reciever_(TSOP22)1.OUT
  N2: Часть1.D10, T1.DQ, R6.Pin_1
  5V: Часть1.5V, IR_Reciever_(TSOP22)1.Vs, Часть3.5V, T1.+Vdd, R6.Pin_0
  N3: Часть1.A5, Часть3.SCL
  N4: Часть1.A4, Часть3.SDA
  3V3: Часть1.3V3, Nokia_5110_LCD_Module1.Vcc
  N5: R1.Pin_1, LED4.cathode
  N6: R2.Pin_1, LED5.cathode
  N7: R3.Pin_0, LED1.cathode
  N8: R4.Pin_0, LED3.cathode
  N9: R5.Pin_1, LED2.cathode

custom parts:
  : Nokia 5110 LCD with 8 pin. It's a 45mm*45mm module part. Description: The Nokia 5110 is a basic graphic LCD screen for lots of applications. It was originally intended for as a cell phone screen. This one is mounted on an easy to solder PCB. It uses the PCD8544 controller. The PCD8544 is a low power CMOS LCD controller/driver, designed to drive a graphic display of 48 rows and 84 columns. All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
  IR Reciever: Basic infrared reciever
  Real Time Clock Module - DS1307 RTC Breakout Board: This a custom designed module for the DS1307 Real Time Clock. The module comes fully assembled and pre-programmed with the current time (ok, so it's our current time - MST). The included Lithium coin cell battery (CR1225 41mAh) will run the module for a minimum of 9 years (17 years typical) without external 5V power. The DS1307 is accessed via the I2C protocol. We've written a test-bed to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
  DS18B20 Temperature Sensor: A DS18B20 temperature sensor
